// Logisim project Gate.circ as structural Verilog: 1 circuit, main circuit main
module main (
  input  NOT_GATE,
  input  in_2,
  input  in_3,
  input  in_4,
  input  in_5,
  input  in_6,
  input  in_7,
  input  in_8,
  input  in_9,
  input  XNOR_GATE,
  input  NAND_GATE,
  input  in_12,
  input  in_13,
  output out_14,
  output out_15,
  output out_16,
  output out_17,
  output out_18,
  output out_19,
  output out_20
);

  not not_1 (out_14, NOT_GATE);
  and and_1 (out_16, in_4, in_5);
  or or_1 (out_18, in_8, in_9);
  nand nand_1 (out_20, NAND_GATE, in_13);
  nor nor_1 (out_15, in_2, in_3);
  xor xor_1 (out_17, in_6, in_7);
  xnor xnor_1 (out_19, XNOR_GATE, in_12);

  // Notes on the sheet:
  //   AND GATE
  //   OR GATE
  //   NOR GATE
  //   XOR GATE
endmodule
