// Logisim project Half Adder.circ as structural Verilog: 1 circuit, main circuit main
module main (
  input  A,
  input  B,
  output SUM,
  output CARRY
);

  xor xor_1 (SUM, A, B);
  and and_1 (CARRY, B, A);

  // Notes on the sheet:
  //   S = A XOR B
  //   C = A AND B
  //   HALF ADDER
endmodule
